# Fritzing sketch Schematic (saved by Fritzing 0.9.3b)
breadboards: 1

parts:
  Part1 = Arduino Uno (Rev3)
  S1 = Pushbutton [package="[THT]"]
  LED1 = smd LED [color="Red (633nm)" package="0603 [SMD]"]
  R1 = Resistor [tolerance=±5% resistance=220 package="0603 [SMD]"]
  R2 = Resistor [tolerance=±5% resistance=220 package="0603 [SMD]"]

nets:
  N1: Part1.D9_PWM, LED1.anode
  N2: Part1.D2, S1.Pin_3, S1.Pin_4, R2.Pin_0
  N3: Part1.3V3, S1.Pin_1, S1.Pin_2
  N4: Part1.GND, R1.Pin_1, R2.Pin_1
  N5: LED1.cathode, R1.Pin_0
