# Fritzing sketch circuit (saved by Fritzing 0.9.3b)
breadboards: 1

parts:
  Part1 = Arduino Uno (Rev3) - ICSP
  U1 = 7-SEGMENT-DISPLAY [package=7-segment-display]
  IC1 = SHIFT REGISTER [package=dil16]
  R1 = Resistor [tolerance=±5% resistance=220 package="1206 [SMD]"]
  R2 = Resistor [tolerance=±5% resistance=220 package="1206 [SMD]"]
  R3 = Resistor [tolerance=±5% resistance=220 package="1206 [SMD]"]
  R4 = Resistor [tolerance=±5% resistance=220 package="1206 [SMD]"]
  R5 = Resistor [tolerance=±5% resistance=220 package="1206 [SMD]"]
  R6 = Resistor [tolerance=±5% resistance=220 package="1206 [SMD]"]
  R7 = Resistor [tolerance=±5% resistance=220 package="1206 [SMD]"]
  R8 = Resistor [tolerance=±5% resistance=220 package="1206 [SMD]"]
  J1 = Piezo Speaker
  S1 = Pushbutton [package="[THT]"]
  R9 = Rotary Potentiometer (Small) [maximum_resistance=100kΩ package=THT]
  R10 = Resistor [tolerance=±5% resistance=10k package="1206 [SMD]"]
  R11 = Resistor [tolerance=±5% resistance=220 package="1206 [SMD]"]

nets:
  N1: Part1.A0, R9.wiper
  N2: Part1.D8, J1.pin2
  N3: Part1.D9_PWM, S1.Pin_1, S1.Pin_2
  N4: Part1.D2, IC1.SCK
  N5: Part1.D3_PWM, IC1.RCK
  N6: Part1.D4, IC1.SER
  5V: Part1.5V, IC1.SCL, IC1.VCC, S1.Pin_4, R9.leg2
  N7: Part1.GND, U1.C, IC1.G, R9.leg1, R10.Pin_1, R11.Pin_1
  N8: U1.E, R6.Pin_1
  N9: U1.D, R8.Pin_1
  N10: U1.G1, R7.Pin_1
  N11: U1.DP, R4.Pin_1
  N12: U1.B, R1.Pin_1
  N13: U1.A, R2.Pin_1
  N14: U1.G2, R3.Pin_1
  N15: U1.G, R5.Pin_1
  N16: IC1.QB, R8.Pin_0
  N17: IC1.QC, R7.Pin_0
  N18: IC1.QD, R5.Pin_0
  N19: IC1.QE, R4.Pin_0
  N20: IC1.QF, R3.Pin_0
  N21: IC1.QG, R2.Pin_0
  N22: IC1.QH, R1.Pin_0
  N23: IC1.QA, R6.Pin_0
  N24: J1.pin1, R11.Pin_0
