# Fritzing sketch Circuit (saved by Fritzing 0.9.3b)
breadboards: 1

parts:
  Part1 = Arduino Uno (Rev3)
  S1 = Tilt Switch [package=THT]
  R1 = Resistor [tolerance=±5% resistance=220 package="0603 [SMD]"]
  LED1 = smd LED [color="Red (633nm)" package="0805 [SMD]"]
  R2 = Resistor [tolerance=±5% resistance=220 package="0603 [SMD]"]
  R3 = Rotary Potentiometer (Small) [maximum_resistance=100kΩ package=THT]

nets:
  N1: Part1.A0, R3.wiper
  N2: Part1.D2, R2.Pin_0
  N3: Part1.D3_PWM, S1.Pin_1, R1.Pin_0
  N4: Part1.5V, R3.leg2
  N5: Part1.GND, S1.Pin_2, LED1.cathode, R3.leg1
  N6: LED1.anode, R2.Pin_1
